// Logisim project 多路选择器型加法器.circ as structural Verilog: 1 circuit, main circuit main
module main (
  input  [7:0] in_1,
  input  in_2,
  input  in_3,
  input  in_4,
  output out_5,
  output [7:0] out_6
);

  wire A, ADD, adder_1_cout, and_1_out, and_2_out, and_3_out, B, clock_1_out, CLR, LDA, LDB,
       multiplexer_1_out, multiplexer_2_out, not_2_out, not_3_out, T2;
  wire [7:0] controlled_buffer_1_out, register_2_q, register_3_q;

  Register #(.width(1)) register_1 (.D(adder_1_cout), .Q(out_5), .clk(and_1_out), .clr(CLR));  // open: en
  and and_1 (and_1_out, ADD, T2);
  and and_2 (and_2_out, LDA, T2);
  assign controlled_buffer_1_out = ADD ? register_3_q : 8'bz;  // Controlled_Buffer controlled_buffer_1
  Register register_2 (.D(in_1), .Q(register_2_q), .clk(and_2_out));  // open: en, clr
  Adder adder_1 (.a(register_2_q), .b(controlled_buffer_1_out), .out(out_6), .cout(adder_1_cout));  // open: cin
  Register register_3 (.D(out_6), .Q(register_3_q), .clk(and_3_out));  // open: en, clr
  and and_3 (and_3_out, T2, LDB);
  Clock clock_1 (.out(clock_1_out));
  xnor xnor_1 (LDA, B, A);
  not not_1 (T2, clock_1_out);
  Multiplexer #(.select(2)) multiplexer_1 (
    .in0(in_2), .in1(in_3), .in2(in_3), .in3(in_3), .out(multiplexer_1_out), .sel({A, B}));  // open: en
  xor xor_1 (LDB, B, A);
  D_Flip_Flop d_ff_1 (.clk(clock_1_out), .D(multiplexer_1_out), .Q(A));  // open: Qn, preset, en, reset
  not not_2 (not_2_out, in_4);
  and and_4 (ADD, B, not_3_out);
  not not_3 (not_3_out, A);
  D_Flip_Flop d_ff_2 (.clk(clock_1_out), .D(multiplexer_2_out), .Q(B));  // open: Qn, preset, en, reset
  Multiplexer #(.select(2)) multiplexer_2 (
    .in0(not_2_out), .in1(in_4), .in2(in_4), .in3(in_4), .out(multiplexer_2_out), .sel({A, B}));  // open: en
  nor nor_1 (CLR, A, B);

  // Notes on the sheet:
  //   T1
endmodule
